// Logisim project TallerLogica-Combinatorios.circ as structural Verilog
module sumador_simple (
  input  A,
  input  B,
  output S,
  output Cout
);

  xor xor_1 (S, A, B);
  and and_1 (Cout, A, B);
endmodule

module sumador_completo (
  input  Cin,
  input  A,
  input  B,
  output S,
  output Cout
);

  wire sumador_simple_1_cout, sumador_simple_1_s, sumador_simple_2_cout;

  sumador_simple sumador_simple_1 (.A(A), .B(B), .S(sumador_simple_1_s), .Cout(sumador_simple_1_cout));
  sumador_simple sumador_simple_2 (.A(Cin), .B(sumador_simple_1_s), .S(S), .Cout(sumador_simple_2_cout));
  xor xor_1 (Cout, sumador_simple_2_cout, sumador_simple_1_cout);
endmodule

module sumador_4 (
  input  Cin,
  input  [3:0] A,
  input  [3:0] B,
  output [3:0] S,
  output Cout
);

  wire sumador_completo_1_cout, sumador_completo_2_cout, sumador_completo_3_cout;

  sumador_completo sumador_completo_1 (.Cin(Cin), .A(A[0]), .B(B[0]), .S(S[0]), .Cout(sumador_completo_1_cout));
  sumador_completo sumador_completo_2 (
    .Cin(sumador_completo_1_cout), .A(A[1]), .B(B[1]), .S(S[1]), .Cout(sumador_completo_2_cout));
  sumador_completo sumador_completo_3 (
    .Cin(sumador_completo_2_cout), .A(A[2]), .B(B[2]), .S(S[2]), .Cout(sumador_completo_3_cout));
  sumador_completo sumador_completo_4 (.Cin(sumador_completo_3_cout), .A(A[3]), .B(B[3]), .S(S[3]), .Cout(Cout));
  Hex_Digit_Display hex_digit_display_1 (.value(S));  // open: dp
endmodule

module comparador_cero (
  input  [3:0] A,
  output Z
);

  wire and_1_out, and_2_out, not_1_out, not_2_out, not_3_out, not_4_out;

  not not_1 (not_1_out, A[0]);
  not not_2 (not_2_out, A[1]);
  not not_3 (not_3_out, A[2]);
  not not_4 (not_4_out, A[3]);
  and and_1 (and_1_out, not_1_out, not_2_out);
  and and_2 (and_2_out, not_3_out, not_4_out);
  and and_3 (Z, and_1_out, and_2_out);
endmodule

module sumador_flags (
  input  Cin,
  input  [3:0] A,
  input  [3:0] B,
  output Z,
  output [3:0] S,
  output C,
  output N,
  output V
);

  wire and_1_out, xnor_1_out, xor_1_out;

  sumador_4 sumador_4_1 (.Cin(Cin), .A(A), .B(B), .S({N, S[2:0]}), .Cout(C));
  and and_1 (and_1_out, A[3], B[3]);
  Hex_Digit_Display hex_digit_display_1 (.value({N, S[2:0]}));  // open: dp
  xor xor_1 (xor_1_out, N, and_1_out);
  xnor xnor_1 (xnor_1_out, A[3], B[3]);
  and and_2 (V, xor_1_out, xnor_1_out);
  comparador_cero comparador_cero_1 (.A({N, S[2:0]}), .Z(Z));

  assign S[3] = N;
endmodule

module incrementador_4 (
  input  [3:0] A,
  output [3:0] S
);

  sumador_4 sumador_4_1 (.A(A), .B(4'b0001), .S(S));  // open: Cin, Cout
  Hex_Digit_Display hex_digit_display_1 (.value(S));  // open: dp
endmodule

module inversor_4 (
  input  [3:0] A,
  input  INV,
  output [3:0] S
);

  wire not_1_out, not_2_out, not_3_out, not_4_out;
  wire [3:0] incrementador_4_1_s, multiplexer_2_out;

  not not_1 (not_1_out, A[0]);
  not not_2 (not_2_out, A[1]);
  not not_3 (not_3_out, A[2]);
  not not_4 (not_4_out, A[3]);
  Multiplexer multiplexer_1 (.in0(A[3]), .in1(not_4_out), .out(multiplexer_2_out[3]), .sel(INV));
  Multiplexer multiplexer_2 (.in0(A[0]), .in1(not_1_out), .out(multiplexer_2_out[0]), .sel(INV));
  Multiplexer multiplexer_3 (.in0(A[1]), .in1(not_2_out), .out(multiplexer_2_out[1]), .sel(INV));
  Multiplexer multiplexer_4 (.in0(A[2]), .in1(not_3_out), .out(multiplexer_2_out[2]), .sel(INV));
  Multiplexer #(.width(4)) multiplexer_5 (.in0(multiplexer_2_out), .in1(incrementador_4_1_s), .out(S), .sel(INV));
  incrementador_4 incrementador_4_1 (.A(multiplexer_2_out), .S(incrementador_4_1_s));
  Hex_Digit_Display hex_digit_display_1 (.value(S));  // open: dp
endmodule

module ALU (
  input  [3:0] A,
  input  [3:0] B,
  input  [1:0] OP,
  output Z,
  output N,
  output V,
  output C,
  output [3:0] S
);

  wire not_1_out, sumador_flags_1_c;
  wire [3:0] and_1_out, inversor_4_1_s, multiplexer_1_out, or_1_out, sumador_flags_1_s;

  inversor_4 inversor_4_1 (.A(B), .INV(OP[0]), .S(inversor_4_1_s));
  buf and_1 (and_1_out[0], A[0]);  // AND_Gate
  and and_2 (and_1_out[1], B[1], A[1]);
  and and_3 (and_1_out[2], B[2], A[2]);
  and and_4 (and_1_out[3], B[3], A[3]);
  or or_1 (or_1_out[0], B[0], A[0]);
  or or_2 (or_1_out[1], B[1], A[1]);
  or or_3 (or_1_out[2], B[2], A[2]);
  or or_4 (or_1_out[3], B[3], A[3]);
  sumador_flags sumador_flags_1 (
    .A(A), .B(inversor_4_1_s), .Z(Z), .S(sumador_flags_1_s), .C(sumador_flags_1_c), .N(N), .V(V));  // open: Cin
  Multiplexer #(.width(4)) multiplexer_1 (.in0(and_1_out), .in1(or_1_out), .out(multiplexer_1_out), .sel(OP[0]));
  Multiplexer multiplexer_2 (.in0(sumador_flags_1_c), .in1(not_1_out), .out(C), .sel(OP[0]));
  not not_1 (not_1_out, sumador_flags_1_c);
  Multiplexer #(.width(4)) multiplexer_3 (.in0(sumador_flags_1_s), .in1(multiplexer_1_out), .out(S), .sel(OP[1]));
  Hex_Digit_Display hex_digit_display_1 (.value(S));  // open: dp
endmodule
